# Fritzing sketch sketchOrchardStation (saved by Fritzing 0.9.3b)
breadboards: 1

parts:
  YwRobot_Power_Supply1 = YwRobot Breadboard Power Supply [part_number=545043]
  SIM800L_BO1 = SIM800L BO
  Componente1 = Arduino Nano (Rev3.0)
  RHT1 = Humidity and Temperature Sensor RHT03  # not connected
  Componente2 = Soil Moisture Sensor  # not connected
  U1 = OV7670 Camera [package=camera_sfv24r-2st_2]  # not connected
  YL-83_-_Detection_Board1 = YL-83 Rain Sensor - Detection Board  # not connected
  YL-83_-_Control_Board1 = YL-83 Rain Sensor - Control Board  # not connected
  YL-83_-_Control_Board2 = YL-83 Rain Sensor - Control Board  # not connected
  DS2 = DS18B20 1-Wire Temperature Sensor Probe Cable  # not connected

nets:
  N1: YwRobot_Power_Supply1.VCC#5, YwRobot_Power_Supply1.VCC#6
  N2: YwRobot_Power_Supply1.VCC#9, YwRobot_Power_Supply1.VCC#10
  N3: YwRobot_Power_Supply1.GND#11, YwRobot_Power_Supply1.GND#12
  N4: YwRobot_Power_Supply1.GND#13, YwRobot_Power_Supply1.GND#14
  N5: SIM800L_BO1.PIN2, Componente1.5V
  N6: SIM800L_BO1.pin_4, Componente1.D3
  N7: SIM800L_BO1.pin_5, Componente1.D2
  N8: SIM800L_BO1.pin_6, Componente1.GND

custom parts:
  YwRobot Breadboard Power Supply: The YwRobot Breadboard Power Supply (MB-V2) has two power rails; they can be 5V or 3V3. Power to the module can be provided through the female USB socket or through the A10 (female) 2.1mm power jack.
  OV7670 Camera: CMOS image sensor
  YL-83 Rain Sensor - Detection Board: The YL-83 is a rain sensor that has more resistance when dry and less resistance when wet. The module runs at 5V.
  YL-83 Rain Sensor - Control Board: The YL-83 is a rain sensor that has more resistance when dry and less resistance when wet. The module runs at 5V.
